# Fritzing sketch diy-gameboy (saved by Fritzing 0.9.3b)
breadboards: 1

parts:
  Part1 = Arduino Uno (Rev3)
  Part2 = Thumb Joystick
  8x8_LED_Modul_mit_MAX1 = 8x8 LED Modul mit MAX7219 [package=THT]

nets:
  N1: Part1.A0, Part2.VERT
  N2: Part1.A1, Part2.HORZ
  N3: Part1.D8, 8x8_LED_Modul_mit_MAX1.CLK_Eingang
  N4: Part1.D9_PWM, 8x8_LED_Modul_mit_MAX1.CS_Eingang
  N5: Part1.D10_PWM/SS, 8x8_LED_Modul_mit_MAX1.DIN_Eingang
  N6: Part1.D12/MISO, Part2.SEL
  GND: Part1.GND, Part2.GND, 8x8_LED_Modul_mit_MAX1.GND_Eingang
  5V: Part1.5V, Part2.VCC, 8x8_LED_Modul_mit_MAX1.VCC_Eingang
